# Fritzing sketch scheme (saved by Fritzing 0.9.5d)

parts:
  LED1 = LED - 5mm [color="Red (633nm)" package="5 mm [THT]"]
  WeMos_D1_Mini_WS2812B_RGB_Shield1 = WeMos D1 Mini WS2812B RGB Shield
  LCD1 = LCD screen
  S1 = Momentary Switch [package=ksa_sealed_tac_switch]
  PCB2 = RTC_DS1302_module
  LCM1602_IIC1 = LCM1602 IIC [part_number="LCM1602 IIC" chip_label="LCM1602 IIC" package="DIP (Dual Inline) [THT]"]
  R1 = Resistor [tolerance=±5% resistance=220 package="2512 [SMD]"]
  R2 = Resistor [tolerance=±5% resistance=220 package="0402 [SMD]"]

nets:
  N1: LED1.cathode, R1.Pin_0
  N2: LED1.anode, WeMos_D1_Mini_WS2812B_RGB_Shield1.D5
  N3: WeMos_D1_Mini_WS2812B_RGB_Shield1.3V3, S1.2
  VCC: WeMos_D1_Mini_WS2812B_RGB_Shield1.5V, PCB2.VCC, LCM1602_IIC1.VCC
  GND: WeMos_D1_Mini_WS2812B_RGB_Shield1.D0, WeMos_D1_Mini_WS2812B_RGB_Shield1.G, PCB2.GND, LCM1602_IIC1.GND, R1.Pin_1, R2.Pin_1
  N4: WeMos_D1_Mini_WS2812B_RGB_Shield1.D1, LCM1602_IIC1.SDA
  N5: WeMos_D1_Mini_WS2812B_RGB_Shield1.D2, LCM1602_IIC1.SCL
  N6: WeMos_D1_Mini_WS2812B_RGB_Shield1.D6, PCB2.RST
  N7: WeMos_D1_Mini_WS2812B_RGB_Shield1.D7, PCB2.DAT
  N8: WeMos_D1_Mini_WS2812B_RGB_Shield1.D8, PCB2.CLK
  VSS: LCD1.VSS, LCM1602_IIC1.VSS
  VDD: LCD1.VDD, LCM1602_IIC1.VDD
  N9: LCD1.V0, LCM1602_IIC1.V0
  N10: LCD1.RS, LCM1602_IIC1.RS
  N11: LCD1.R/W, LCM1602_IIC1.RW
  N12: LCD1.E, LCM1602_IIC1.E
  N13: LCD1.DB0, LCM1602_IIC1.D0
  N14: LCD1.DB1, LCM1602_IIC1.D1
  N15: LCD1.DB2, LCM1602_IIC1.D2
  N16: LCD1.DB3, LCM1602_IIC1.D3
  N17: LCD1.DB4, LCM1602_IIC1.D4
  N18: LCD1.DB5, LCM1602_IIC1.D5
  N19: LCD1.DB6, LCM1602_IIC1.D6
  N20: LCD1.DB7, LCM1602_IIC1.D7
  N21: LCD1.LED+, LCM1602_IIC1.A
  N22: LCD1.LED-, LCM1602_IIC1.K
  N23: S1.3, R2.Pin_0

notes:
  Подсветка
  Какой-то диод, главное красный!
  10k
  200-1k+
  LCD 16x02
  RTC DS1302
  03:00:00
  Status: 500
  WEMOS D1 mini

custom parts:
  RTC_DS1302_module: Arduino module DS1302 SPI Real Time Clock
  LCM1602 IIC: I2C-Module to use a 1602 or 2004 LCD on with the wire.h libory Serial LCD Modul
